# Fritzing sketch Fritizing Question 3 (saved by Fritzing 0.9.5d)
breadboards: 1

parts:
  U1 = ESP32-38PinWide [part_number=ESP32-38PinWide]
  M1 = fc-51 [package=THT]
  Part1 = LCD1602-I2C

nets:
  N1: U1.3.3, M1.pin3, Part1.VCC
  N2: U1.GPIO35, Part1.SDA
  N3: U1.GPIO25, Part1.SCL
  N4: U1.GPIO26, M1.pin1
  GND: U1.GND, M1.pin2, Part1.GND

custom parts:
  ESP32-38PinWide: Generic 38-Pin ESP32 with wide format (only access to one side of pins on a breadboard) based on Stephen Lilley's HiLetgo ESP-WROOM-32 ESP32 ESP-32S Development Board.
  fc-51: Fc-51 Infrared Obstacle Avoidance Proximity Sensor module. IR transmitter led, receiver LED, lm393 compaitor and a pot. 3.3 V to 5V power.
  LCD1602-I2C: A standard character display, usually with 2x16 characters. Comes in many colors with LCM1602 IIC attached.
