# Fritzing sketch Fritizing Question 4 (saved by Fritzing 0.9.5d)
breadboards: 1

parts:
  U1 = ESP32-38PinWide [part_number=ESP32-38PinWide]
  J1 = Basic Servo
  LED1 = smd LED [color="Red (633nm)" package="1206 [SMD]"]
  S1 = Pushbutton [package="[THT]"]
  R1 = Resistor [tolerance=±5% resistance=220 package="2512 [SMD]"]
  J2 = Piezo Speaker
  R2 = Photocell (LDR) [package=THT]
  R3 = Resistor [tolerance=±5% resistance=1000 package="0805 [SMD]"]

nets:
  N1: U1.3.3, J1.vcc, R2.pin_1
  N2: U1.GPIO35, R2.pin_0, R3.Pin_1
  N3: U1.GPIO32, J2.pin2
  N4: U1.GPIO25, R1.Pin_1
  N5: U1.GPIO26, J1.pulse
  N6: U1.GPIO27, S1.Pin_1, S1.Pin_2
  GND: U1.GND, J1.gnd, LED1.cathode, S1.Pin_3, S1.Pin_4, J2.pin1, R3.Pin_0
  N7: LED1.anode, R1.Pin_0

custom parts:
  ESP32-38PinWide: Generic 38-Pin ESP32 with wide format (only access to one side of pins on a breadboard) based on Stephen Lilley's HiLetgo ESP-WROOM-32 ESP32 ESP-32S Development Board.
