# Fritzing sketch Fritizing Question 5 (saved by Fritzing 0.9.5d)
breadboards: 1

parts:
  U1 = ESP32-38PinWide [part_number=ESP32-38PinWide]
  M1 = fc-51 [package=THT]
  J1 = Piezo Speaker
  J2 = Basic Servo
  LED1 = smd LED [color="Red (633nm)" package="0805 [SMD]"]
  R1 = Photocell (LDR) [package=THT]
  S1 = Pushbutton [package="[THT]"]
  Part1 = LCD1602-I2C
  R2 = Resistor [tolerance=±5% resistance=220 package="0805 [SMD]"]
  R3 = Resistor [tolerance=±5% resistance=10000 package="2512 [SMD]"]

nets:
  VCC: U1.3.3, M1.pin3, J2.vcc, R1.pin_1, Part1.VCC
  N1: U1.GPIO35, Part1.SCL
  N2: U1.GPIO32, Part1.SDA
  N3: U1.GPIO33, J1.pin2
  N4: U1.GPIO25, J2.pulse
  N5: U1.GPIO26, S1.Pin_1, S1.Pin_2
  N6: U1.GPIO27, R2.Pin_1
  N7: U1.GPIO14, M1.pin1
  N8: U1.GPIO12, R1.pin_0, R3.Pin_1
  GND: U1.GND, M1.pin2, J1.pin1, J2.gnd, LED1.cathode, S1.Pin_3, S1.Pin_4, Part1.GND, R3.Pin_0
  N9: LED1.anode, R2.Pin_0

custom parts:
  ESP32-38PinWide: Generic 38-Pin ESP32 with wide format (only access to one side of pins on a breadboard) based on Stephen Lilley's HiLetgo ESP-WROOM-32 ESP32 ESP-32S Development Board.
  fc-51: Fc-51 Infrared Obstacle Avoidance Proximity Sensor module. IR transmitter led, receiver LED, lm393 compaitor and a pot. 3.3 V to 5V power.
  LCD1602-I2C: A standard character display, usually with 2x16 characters. Comes in many colors with LCM1602 IIC attached.
