# Fritzing sketch project1 (saved by Fritzing 1.0.1rc)
breadboards: 1

parts:
  U1 = ESP32S-HiLetgo [part_number=ESP32S-HiLetgo]
  M1 = fc-51 [package=THT]
  J1 = Basic Servo

nets:
  N1: U1.GPIO11, M1.pin2, J1.vcc
  VIN: U1.VIN, M1.pin3, J1.gnd
  N2: U1.GPIO8, J1.pulse
  N3: U1.GPIO15, M1.pin1

custom parts:
  ESP32S-HiLetgo: HiLetgo ESP-WROOM-32 ESP32 ESP-32S Development Board 2.4GHz Dual-Mode WiFi + Bluetooth Dual Cores Microcontroller The ESP32 integrated with Antenna switches, RF Balun, power amplifiers, low-noise amplifiers, filters, and management modules, and the entire solution occupies the least area of PCB. 2.4 GHz Wi-Fi plus Bluetooth dual-mode chip, with TSMC Ultra-low power consumption 40nm technology,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
