# Fritzing sketch Task 1  (saved by Fritzing 0.9.3b)
breadboards: 1

parts:
  M1 = ESP32-Nodemcu-32s [part_number=ESP32-Nodemcu-32s]
  Part1 = LCD1602-I2C

nets:
  3V3: M1.3V3, Part1.VCC
  N1: M1.GPIO12, Part1.GND
  N2: M1.GPIO21, Part1.SDA
  N3: M1.GPIO22, Part1.SCL

custom parts:
  ESP32-Nodemcu-32s: The DOIT Esp32 DevKit v1 is one of the development board created by DOIT to evaluate the ESP-WROOM-32 module. It is based on the ESP32 microcontroller that boasts Wifi, Bluetooth, Ethernet and Low Power support all in a single chip. This module is 42pins long (2x21) and 11 pins width.
  LCD1602-I2C: A standard character display, usually with 2x16 characters. Comes in many colors with LCM1602 IIC attached.
