# Fritzing sketch Task 2  (saved by Fritzing 0.9.3b)
breadboards: 1

parts:
  M1 = ESP32-Nodemcu-32s [part_number=ESP32-Nodemcu-32s]
  LED2 = LED - 3mm [color="Yellow (585nm)" package="3 mm [THT]"]
  LED3 = LED - 3mm [color="Red (633nm)" package="3 mm [THT]"]
  R1 = Resistor [tolerance=±5% resistance=220 package="0402 [SMD]"]
  R2 = Resistor [tolerance=±5% resistance=220 package="0402 [SMD]"]

nets:
  N1: M1.GPIO12, R2.Pin_0
  N2: M1.GND#31, R1.Pin_0
  N3: M1.GPIO21, LED2.anode
  N4: M1.GPIO22, LED3.anode
  N5: LED2.cathode, R1.Pin_1
  N6: LED3.cathode, R2.Pin_1

custom parts:
  ESP32-Nodemcu-32s: The DOIT Esp32 DevKit v1 is one of the development board created by DOIT to evaluate the ESP-WROOM-32 module. It is based on the ESP32 microcontroller that boasts Wifi, Bluetooth, Ethernet and Low Power support all in a single chip. This module is 42pins long (2x21) and 11 pins width.
