# Fritzing sketch Task 3  (saved by Fritzing 0.9.3b)
breadboards: 1

parts:
  R2 = Rotary Potentiometer (Small) [maximum_resistance=100kΩ package=THT]
  M1 = ESP32-Nodemcu-32s [part_number=ESP32-Nodemcu-32s]

nets:
  N1: R2.leg1, R2.wiper, M1.GPIO34, M1.GND#13
  N2: R2.leg2, M1.3V3

custom parts:
  ESP32-Nodemcu-32s: The DOIT Esp32 DevKit v1 is one of the development board created by DOIT to evaluate the ESP-WROOM-32 module. It is based on the ESP32 microcontroller that boasts Wifi, Bluetooth, Ethernet and Low Power support all in a single chip. This module is 42pins long (2x21) and 11 pins width.
