# Fritzing sketch Task 4  (saved by Fritzing 0.9.3b)
breadboards: 1

parts:
  M1 = fc-51 [package=THT]
  M2 = ESP32-Nodemcu-32s [part_number=ESP32-Nodemcu-32s]
  J1 = Basic Servo

nets:
  N1: M1.pin1, M2.GPIO32
  N2: M1.pin2, M2.GND#13
  N3: M1.pin3, M2.3V3
  5V: M2.5V, J1.vcc
  N4: M2.GPIO2, J1.pulse
  N5: M2.GND#31, J1.gnd

custom parts:
  ESP32-Nodemcu-32s: The DOIT Esp32 DevKit v1 is one of the development board created by DOIT to evaluate the ESP-WROOM-32 module. It is based on the ESP32 microcontroller that boasts Wifi, Bluetooth, Ethernet and Low Power support all in a single chip. This module is 42pins long (2x21) and 11 pins width.
