# Fritzing sketch Task 7 (saved by Fritzing 0.9.3b)
breadboards: 1

parts:
  M1 = ESP32-Nodemcu-32s [part_number=ESP32-Nodemcu-32s]
  M2 = fc-51 [package=THT]

nets:
  N1: M1.3V3, M2.pin3
  N2: M1.GPIO12, M2.pin2
  N3: M1.GPIO10, M2.pin1

custom parts:
  ESP32-Nodemcu-32s: The DOIT Esp32 DevKit v1 is one of the development board created by DOIT to evaluate the ESP-WROOM-32 module. It is based on the ESP32 microcontroller that boasts Wifi, Bluetooth, Ethernet and Low Power support all in a single chip. This module is 42pins long (2x21) and 11 pins width.
